# Fritzing sketch ApproxyClock (saved by Fritzing 0.8.7b)
circuit board: 16cm x 10cm
breadboards: 2

parts:
  VCC1 = 4 x AAA Battery Mount
  A1 = atmega328 [package=dip]
  C2 = Capacitor [package=cap-pth-small2]
  C1 = Capacitor [package=cap-pth-small2]
  Y1 = CRYSTAL [package=crystal-smd-10.5x4.8-2pin]
  RRST = Resistor [tolerance=±5% resistance=10k package=THT]
  LED1 = RGB LED (com. cathode, rbg) [package="5 mm [THT]"]
  LED2 = RGB LED (com. cathode, rbg) [package="5 mm [THT]"]
  R1 = Resistor [tolerance=±5% resistance=1k package=THT]
  R2 = Resistor [tolerance=±5% resistance=1k package=THT]
  R3 = Resistor [tolerance=±5% resistance=1k package=THT]
  R4 = Resistor [tolerance=±5% resistance=1k package=THT]
  R5 = Resistor [tolerance=±5% resistance=1k package=THT]
  R6 = Resistor [tolerance=±5% resistance=1k package=THT]

nets:
  N1: VCC1.-, A1.GND, C2.2, C1.2, RRST.Pin_1, LED1.common_cathode, LED2.common_cathode
  N2: VCC1.+, A1.RESET, A1.VCC, A1.D7, A1.AVCC, A1.AREF, RRST.Pin_0
  N3: A1.D3_(PWM), R2.Pin_0
  N4: A1.XLAT1, C1.1, Y1.1
  N5: A1.XLAT2, C2.1, Y1.2
  N6: A1.D5_(PWM), R1.Pin_0
  N7: A1.D6_(PWM), R3.Pin_0
  N8: A1.D9_(PWM), R6.Pin_0
  N9: A1.D10_(PWM), R4.Pin_0
  N10: A1.D11_(PWM), R5.Pin_0
  N11: LED1.red_anode, R1.Pin_1
  N12: LED1.blue_anode, R2.Pin_1
  N13: LED1.green_anode, R3.Pin_1
  N14: LED2.red_anode, R4.Pin_1
  N15: LED2.blue_anode, R6.Pin_1
  N16: LED2.green_anode, R5.Pin_1

notes:
  Capacitors: 22 pF
  Crystal: 16 MHz
  RRST: Pull-up resistance for reset
  Followed the same wiring as the RGB LED supplied by Fritzing, which is not the RGB LED I use
